# Fritzing sketch schematics (saved by Fritzing 0.9.10b)
breadboards: 1

parts:
  Raspberry_Pi_1 = Raspberry Pi 3 [part_number=RPI-3-V1.2]  # not connected
  VCC1 = 4 x AAA Battery Mount
  LED1 = LED - 5mm [color="Red (633nm)" current=0.030 package="5 mm [THT]"]
  WeMos_D1_Mini_Relay_Shield1 = WeMos D1 Mini Relay Shield

nets:
  N1: VCC1.-, LED1.cathode
  N2: VCC1.+, WeMos_D1_Mini_Relay_Shield1.NC
  N3: LED1.anode, WeMos_D1_Mini_Relay_Shield1.COM
